# Fritzing sketch pcb (saved by Fritzing 0.9.2b)
circuit board: 2.53194cm x 2.85414cm
breadboards: 1

parts:
  BMP180 = Barometric Pressure Sensor - BMP085 Breakout
  ESP = ESP8266 WiFi Module [part_number=ESP8266]
  +_-_R_T = Header 4 [package=molex-1x4_lock]

nets:
  3.3V: BMP180.VCC, ESP.VCC, +_-_R_T.1
  GND: BMP180.GND, ESP.GND, +_-_R_T.2
  N1: BMP180.SCL, ESP.GPIO_5
  N2: BMP180.SDA, ESP.GPIO_4
  N3: ESP.RXD, +_-_R_T.3
  N4: ESP.TXD, +_-_R_T.4
  N5: ESP.GPIO_16, ESP.REST

custom parts:
  ESP8266 WiFi Module: Generic WiFi Module based on the ESP8266 with onboard PCB antenna and UART communications
