# Fritzing sketch watering (saved by Fritzing 0.9.2b)
circuit board: 4.16278cm x 4.94356cm
breadboards: 1

parts:
  U1 = ESP8266 WiFi Module [part_number=ESP8266]
  U2 = Voltage Regulator - 3.3V [package="TO220 [THT]"]
  Part1 = Motor Driver 1A Dual TB6612FNG
  R1 = Resistor [tolerance=±5% resistance=10k package=THT]
  JP2 = Header 5x2 [package=avr_icsp]

nets:
  RXD: U1.RXD, JP2.8
  3.3V: U1.VCC, U2.output_voltage, Part1.VCC, R1.Pin_0
  N1: U1.CH_PD, R1.Pin_1
  GND: U1.GND, U2.GND, Part1.GND, JP2.2
  TXD: U1.TXD, JP2.7
  PWM_A: U1.GPIO_4, Part1.PWMA
  PWM_B: U1.GPIO_5, Part1.PWMB
  N2: U1.GPIO_16, U1.REST
  +6VDC/6V: U2.input_voltage, Part1.VM, JP2.1
  MOTOR+/MOTOR-: Part1.A02, Part1.A01, JP2.9, JP2.10

custom parts:
  ESP8266 WiFi Module: Generic WiFi Module based on the ESP8266 with onboard PCB antenna and UART communications
